# Fritzing sketch unijoysticle (saved by Fritzing 0.9.2b)
breadboards: 1

parts:
  U1 = NodeMCU V1.0
  74HC1 = DIP - 14 pins [chip_label=4066 package="DIP (Dual Inline) [THT]"]
  74HC2 = DIP - 14 pins [chip_label=4066 package="DIP (Dual Inline) [THT]"]
  X2 = DB9 Connector [package=db9]
  74HC3 = DIP - 14 pins [chip_label=4066 package="DIP (Dual Inline) [THT]"]
  X3 = DB9 Connector [package=db9]

nets:
  N1: U1.D0, 74HC2.1C
  N2: U1.D1, 74HC2.2C
  N3: U1.D2, 74HC2.3C
  N4: U1.D3, 74HC2.4C
  N5: U1.D4, 74HC3.1C
  GND: U1.GND, 74HC1.GND, 74HC2.GND, 74HC3.GND
  N6: U1.D5, 74HC1.1C
  N7: U1.D6, 74HC1.2C
  N8: U1.D7, 74HC1.3C
  N9: U1.D8, 74HC1.4C
  N10: U1.RX, 74HC3.2C
  VCC: U1.3V3, 74HC1.Vcc, 74HC2.Vcc, 74HC3.Vcc
  N11: 74HC1.1A, X2.5
  N12: 74HC1.1B, 74HC1.2B, 74HC2.1B, 74HC2.2B, X2.2, 74HC3.1B, 74HC3.2B
  N13: 74HC1.2A, X2.6
  N14: 74HC1.3A, X2.7
  N15: 74HC1.3B, 74HC1.4B, 74HC2.3B, 74HC2.4B, X3.2
  N16: 74HC1.4A, X2.8
  N17: 74HC2.1A, X3.5
  N18: 74HC2.2A, X3.6
  N19: 74HC2.3A, X3.7
  N20: 74HC2.4A, X3.8
  N21: X2.4, 74HC3.2A
  N22: 74HC3.1A, X3.4

notes:
  UniJoystiCle v0.2
  Joy Port #1
  Joy Port #2

custom parts:
  NodeMCU V1.0: ESP9266 based NodeMCU
  DIP - 14 pins: Quadruple bilateral analog switch
